// Logisim project labo_checksum_VanHove.circ as structural Verilog: 9 circuits, main circuit Add1bit
module Add1bit (
  input  a_i,
  input  b_i,
  input  c_i,
  output r_o,
  output c_o
);

  wire and_1_out, and_2_out, and_3_out, xor_1_out;

  xor xor_1 (xor_1_out, a_i, b_i);
  and and_1 (and_1_out, a_i, b_i);
  and and_2 (and_2_out, a_i, c_i);
  and and_3 (and_3_out, b_i, c_i);
  xor xor_2 (r_o, xor_1_out, c_i);
  or or_1 (c_o, and_1_out, and_2_out, and_3_out);

  // Notes on the sheet:
  //   Attention, votre version de Logisim
  //   ne contient pas de tracker. Si vous
  //   enregistrez votre projet, toutes les
  //   informations du tracker seront
  //   définitivement effacées.
endmodule

module Add4bit (
  input  c_i,
  input  [3:0] a_i,
  input  [3:0] b_i,
  output [3:0] r_o,
  output c_o
);

  wire Add1b_1_c_o, Add1b_2_c_o, Add1b_3_c_o;

  Add1bit Add1b_1 (.a_i(a_i[0]), .b_i(b_i[0]), .c_i(c_i), .r_o(r_o[0]), .c_o(Add1b_1_c_o));
  Add1bit Add1b_2 (.a_i(a_i[1]), .b_i(b_i[1]), .c_i(Add1b_1_c_o), .r_o(r_o[1]), .c_o(Add1b_2_c_o));
  Add1bit Add1b_3 (.a_i(a_i[2]), .b_i(b_i[2]), .c_i(Add1b_2_c_o), .r_o(r_o[2]), .c_o(Add1b_3_c_o));
  Add1bit Add1b_4 (.a_i(a_i[3]), .b_i(b_i[3]), .c_i(Add1b_3_c_o), .r_o(r_o[3]), .c_o(c_o));

  // Notes on the sheet:
  //   Attention, votre version de Logisim
  //   ne contient pas de tracker. Si vous
  //   enregistrez votre projet, toutes les
  //   informations du tracker seront
  //   définitivement effacées.
endmodule

module Sub4bit (
  input  [3:0] a_i,
  input  [3:0] b_i,
  output [3:0] r_o,
  output c_o
);

  wire [3:0] xor_1_out;

  assign xor_1_out = b_i ^ 4'b1111;  // XOR_Gate xor_1, 4 bits wide
  Add4bit Add4b_1 (.c_i(1'b1), .a_i(a_i), .b_i(xor_1_out), .r_o(r_o), .c_o(c_o));

  // Notes on the sheet:
  //   Attention, votre version de Logisim
  //   ne contient pas de tracker. Si vous
  //   enregistrez votre projet, toutes les
  //   informations du tracker seront
  //   définitivement effacées.
endmodule

module AddSub4bit (
  input  sel_i,
  input  [3:0] a_i,
  input  [3:0] b_i,
  output [3:0] r_o,
  output c_o
);

  wire [3:0] xor_1_out;

  assign xor_1_out = {4{sel_i}} ^ b_i;  // XOR_Gate xor_1, 4 bits wide
  Add4bit add4b_1 (.c_i(sel_i), .a_i(a_i), .b_i(xor_1_out), .r_o(r_o), .c_o(c_o));

  // Notes on the sheet:
  //   Attention, votre version de Logisim
  //   ne contient pas de tracker. Si vous
  //   enregistrez votre projet, toutes les
  //   informations du tracker seront
  //   définitivement effacées.
endmodule

module Add8bit (
  input  c_i,
  input  [7:0] a_i,
  input  [7:0] b_i,
  output [7:0] r_o,
  output c_o
);

  wire add4b_1_c_o;

  Add4bit add4b_1 (.c_i(c_i), .a_i(a_i[3:0]), .b_i(b_i[3:0]), .r_o(r_o[3:0]), .c_o(add4b_1_c_o));
  Add4bit add4b_2 (.c_i(add4b_1_c_o), .a_i(b_i[7:4]), .b_i(a_i[7:4]), .r_o(r_o[7:4]), .c_o(c_o));

  // Notes on the sheet:
  //   Attention, votre version de Logisim
  //   ne contient pas de tracker. Si vous
  //   enregistrez votre projet, toutes les
  //   informations du tracker seront
  //   définitivement effacées.
endmodule

module AddSub8bit (
  input  sel_i,
  input  [7:0] a_i,
  input  [7:0] b_i,
  output [7:0] r_o,
  output c_o
);

  wire [7:0] xor_1_out;

  assign xor_1_out = {8{sel_i}} ^ b_i;  // XOR_Gate xor_1, 8 bits wide
  Add8bit add8b_1 (.c_i(sel_i), .a_i(a_i), .b_i(xor_1_out), .r_o(r_o), .c_o(c_o));

  // Notes on the sheet:
  //   Attention, votre version de Logisim
  //   ne contient pas de tracker. Si vous
  //   enregistrez votre projet, toutes les
  //   informations du tracker seront
  //   définitivement effacées.
endmodule

module Checksum (
  input  [7:0] a_i,
  input  [7:0] b_i,
  input  [7:0] c_i,
  output [7:0] r_o
);

  wire [7:0] Add_ab_r_o, Add_abc_r_o, not_1_out;

  Add8bit Add_ab (.c_i(1'b0), .a_i(a_i), .b_i(b_i), .r_o(Add_ab_r_o));  // open: c_o
  Add8bit Add_abc (.c_i(1'b0), .a_i(Add_ab_r_o), .b_i(c_i), .r_o(Add_abc_r_o));  // open: c_o
  assign not_1_out = ~Add_abc_r_o;  // NOT_Gate not_1, 8 bits wide
  Add8bit Add_1 (.c_i(1'b0), .a_i(not_1_out), .b_i(8'h1), .r_o(r_o));  // open: c_o

  // Notes on the sheet:
  //   Attention, votre version de Logisim
  //   ne contient pas de tracker. Si vous
  //   enregistrez votre projet, toutes les
  //   informations du tracker seront
  //   définitivement effacées.
endmodule

module VerifyIntegrity (
  input  [7:0] a_i,
  input  [7:0] b_i,
  input  [7:0] c_i,
  input  [7:0] d_i,
  output verif_checksum_o
);

  wire [7:0] Add_ab_r_o, add_abcd_r_o, Add_cd_r_o, not_1_out;

  Add8bit Add_ab (.c_i(1'b0), .a_i(a_i), .b_i(b_i), .r_o(Add_ab_r_o));  // open: c_o
  Add8bit Add_cd (.c_i(1'b0), .a_i(c_i), .b_i(d_i), .r_o(Add_cd_r_o));  // open: c_o
  Add8bit add_abcd (.c_i(1'b0), .a_i(Add_ab_r_o), .b_i(Add_cd_r_o), .r_o(add_abcd_r_o));  // open: c_o
  assign not_1_out = ~add_abcd_r_o;  // NOT_Gate not_1, 8 bits wide
  and and_1 (verif_checksum_o, not_1_out[0], not_1_out[1], not_1_out[2], not_1_out[3], not_1_out[4], not_1_out[5], not_1_out[6], not_1_out[7]);

  // Notes on the sheet:
  //   Attention, votre version de Logisim
  //   ne contient pas de tracker. Si vous
  //   enregistrez votre projet, toutes les
  //   informations du tracker seront
  //   définitivement effacées.
endmodule

module FPGA (
);

  wire [7:0] B1_out, checkFPGA_r_o;

  Button B1 (.out(B1_out[0]));
  Button B2 (.out(B1_out[1]));
  Button B3 (.out(B1_out[2]));
  Button B4 (.out(B1_out[3]));
  Button B5 (.out(B1_out[4]));
  Button B6 (.out(B1_out[5]));
  Button B7 (.out(B1_out[6]));
  Button B8 (.out(B1_out[7]));
  Checksum checkFPGA (.a_i(8'h1), .b_i(8'h5), .c_i(B1_out), .r_o(checkFPGA_r_o));
  LED L1 (.in(checkFPGA_r_o[0]));
  LED L2 (.in(checkFPGA_r_o[1]));
  LED L3 (.in(checkFPGA_r_o[2]));
  LED L4 (.in(checkFPGA_r_o[3]));
  LED L5 (.in(checkFPGA_r_o[4]));
  LED L6 (.in(checkFPGA_r_o[5]));
  LED L7 (.in(checkFPGA_r_o[6]));
  LED L8 (.in(checkFPGA_r_o[7]));

  // Notes on the sheet:
  //   Attention, votre version de Logisim
  //   ne contient pas de tracker. Si vous
  //   enregistrez votre projet, toutes les
  //   informations du tracker seront
  //   définitivement effacées.
endmodule
